# Fritzing sketch tah_testbed_sch (saved by Fritzing 0.8.7b)
breadboards: 1

parts:
  74LS151 = IC, DIP package, 16 pins [chip_label=74ALS151]
  Part1 = Arduino Leonardo (Rev3b)
  Raspberry_Pi_B_rev1 = Raspberry Pi B rev2
  U1 = 74HC4067 [package=ssop24]
  U2 = LCD-16X2 [package=lcd-16x2]
  R1 = Trimmer Potentiometer [maximum_resistance=10kΩ package=THT]

nets:
  N1: 74LS151.pin1, Part1.A3
  N2: 74LS151.pin2, Part1.A2
  N3: 74LS151.pin3, Part1.A1
  N4: 74LS151.pin4, Part1.A0
  3V3: 74LS151.pin5, 74LS151.pin16, Raspberry_Pi_B_rev1.3V3, U1.COM, U1.VCC
  GND: 74LS151.pin7, 74LS151.pin8, Raspberry_Pi_B_rev1.GND, U1.GND, U1.EN
  N5: 74LS151.pin9, Raspberry_Pi_B_rev1.GPIO_15, U1.S2
  N6: 74LS151.pin10, Raspberry_Pi_B_rev1.GPIO_3, U1.S1
  N7: 74LS151.pin11, Raspberry_Pi_B_rev1.GPIO_2, U1.S0
  N8: 74LS151.pin14, Part1.A5
  N9: 74LS151.pin15, Part1.A4
  N10: Part1.D2/SDA, U1.CHAN11
  N11: Part1.D3_PWM/SCL, Part1.SCL, U1.CHAN10
  N12: Part1.D4/A6, U1.CHAN9
  N13: Part1.D5_PWM, U1.CHAN8
  N14: Part1.D6_PWM/A7, U1.CHAN7
  N15: Part1.D7, U1.CHAN6
  N16: Part1.D8/A8, U1.CHAN5
  N17: Part1.D9_PWM/A9, U1.CHAN4
  N18: Part1.D10_PWM/A10, U1.CHAN3
  N19: Part1.D11_PWM, U1.CHAN2
  N20: Part1.D12/A11, U1.CHAN1
  N21: Part1.D13_PWM, U1.CHAN0
  N22: Raspberry_Pi_B_rev1.GPIO_14, U1.S3
  N23: Raspberry_Pi_B_rev1.GPIO_18, U2.DB7
  N24: Raspberry_Pi_B_rev1.GPIO_4, U2.DB6
  N25: Raspberry_Pi_B_rev1.GPIO_24, U2.DB5
  N26: Raspberry_Pi_B_rev1.GPIO_25, U2.DB4
  N27: Raspberry_Pi_B_rev1.GPIO_8, U2.E
  N28: Raspberry_Pi_B_rev1.GPIO_7, U2.RS
  GND_2: U2.VSS, U2.A, R1.leg1
  N29: U2.VO, R1.leg2
  5V: U2.K, R1.wiper
